// Logisim project 2351520-毛星博-6.1_1.circ as structural Verilog: 1 circuit, main circuit main
module main (
  input  in_1,
  input  in_2,
  output out_3,
  output out_4,
  output out_5
);

  and and_1 (out_3, in_1, in_2);
  or or_1 (out_4, in_1, in_2);
  not nor_1 (out_5, in_1);  // NOR_Gate
endmodule
