// Logisim project 2351520-毛星博-6.1_4.circ as structural Verilog: 1 circuit, main circuit main
module main (
  input  in_1,
  input  in_2,
  output out_3
);

  assign out_3 = in_2 ? in_1 : 1'bz;  // Controlled_Buffer controlled_buffer_1
endmodule
