// Logisim project 6.7_1.circ as structural Verilog: 1 circuit, main circuit main
module main (
  input  CLK,
  input  rst,
  output [2:0] out_3
);

  wire and_1_out, not_1_out;

  J_K_Flip_Flop j_k_ff_1 (.J(1'b1), .clk(CLK), .K(1'b1), .Q(out_3[0]), .reset(not_1_out));  // open: Qn, preset, en
  not not_1 (not_1_out, rst);
  J_K_Flip_Flop j_k_ff_2 (
    .J(out_3[0]), .clk(CLK), .K(out_3[0]), .Q(out_3[1]), .reset(not_1_out));  // open: Qn, preset, en
  and and_1 (and_1_out, out_3[0], out_3[1]);
  J_K_Flip_Flop j_k_ff_3 (
    .J(and_1_out), .clk(CLK), .K(and_1_out), .Q(out_3[2]), .reset(not_1_out));  // open: Qn, preset, en
endmodule
