// Logisim project 6.3.1(1).circ as structural Verilog: 1 circuit, main circuit main
module main (
  input  [2:0] iData,
  input  [1:0] Ena,
  output [7:0] oData
);

  wire not_1_out, not_2_out, not_3_out, not_4_out, or_1_out;

  not not_1 (not_1_out, Ena[1]);
  not not_2 (not_2_out, iData[0]);
  not not_3 (not_3_out, iData[1]);
  not not_4 (not_4_out, iData[2]);
  or or_1 (or_1_out, Ena[0], not_1_out);
  or or_2 (oData[0], iData[2], iData[1], or_1_out, iData[0]);
  or or_3 (oData[1], iData[2], iData[0], or_1_out, not_2_out);
  or or_4 (oData[2], iData[2], not_3_out, or_1_out, iData[0]);
  or or_5 (oData[3], iData[2], not_3_out, or_1_out, not_2_out);
  or or_6 (oData[4], not_4_out, or_1_out, iData[1], iData[0]);
  or or_7 (oData[5], not_4_out, or_1_out, iData[1], not_2_out);
  or or_8 (oData[6], not_4_out, or_1_out, not_3_out, iData[0]);
  or or_9 (oData[7], not_4_out, or_1_out, not_3_out, not_2_out);

  // Notes on the sheet:
  //   D2
  //   G1
  //   D1
  //   D0
  //   G2
  //   F7F6F5F4F3F2F1F0
endmodule
