// Logisim project 6.3.3.circ as structural Verilog: 1 circuit, main circuit main
module main (
  input  [7:0] iData,
  output [2:0] oData
);

  or or_1 (oData[2], iData[7], iData[6], iData[5], iData[4]);
  or or_2 (oData[1], iData[7], iData[6], iData[3], iData[2]);
  or or_3 (oData[0], iData[7], iData[5], iData[3], iData[1]);

  // Notes on the sheet:
  //   D7----------D0
  //   Y2--Y0
endmodule
