// Logisim project 4位4选1数据选择器.circ as structural Verilog: 1 circuit, main circuit main
module main (
  input  in_1,
  input  in_2,
  input  [3:0] in_3,
  input  [3:0] in_4,
  input  [3:0] in_5,
  input  [3:0] in_6,
  output out_7,
  output out_8,
  output out_9,
  output out_10
);

  wire and_1_out, and_2_out, and_3_out, and_4_out, and_5_out, and_6_out, and_7_out, and_8_out, and_9_out,
       and_10_out, and_11_out, and_12_out, and_13_out, and_14_out, and_15_out, and_16_out, not_1_out,
       not_2_out, not_3_out, not_4_out, not_5_out, not_6_out, not_7_out, not_8_out;

  not not_1 (not_1_out, in_1);
  not not_2 (not_2_out, in_2);
  not not_3 (not_3_out, in_1);
  not not_4 (not_4_out, in_2);
  not not_5 (not_5_out, in_1);
  not not_6 (not_6_out, in_2);
  not not_7 (not_7_out, in_1);
  not not_8 (not_8_out, in_2);
  and and_1 (and_1_out, in_3[0], not_2_out, not_1_out);
  and and_2 (and_2_out, in_4[0], not_2_out, in_1);
  and and_3 (and_3_out, in_5[0], in_2, not_1_out);
  and and_4 (and_4_out, in_6[0], in_2, in_1);
  and and_5 (and_5_out, in_3[1], not_4_out, not_3_out);
  and and_6 (and_6_out, in_4[1], not_4_out, in_1);
  and and_7 (and_7_out, in_5[1], in_2, not_3_out);
  and and_8 (and_8_out, in_6[1], in_2, in_1);
  and and_9 (and_9_out, in_3[2], not_6_out, not_5_out);
  and and_10 (and_10_out, in_4[2], not_6_out, in_1);
  and and_11 (and_11_out, in_5[2], in_2, not_5_out);
  and and_12 (and_12_out, in_6[2], in_2, in_1);
  and and_13 (and_13_out, in_3[3], not_8_out, not_7_out);
  and and_14 (and_14_out, in_4[3], not_8_out, in_1);
  and and_15 (and_15_out, in_5[3], in_2, not_7_out);
  and and_16 (and_16_out, in_6[3], in_2, in_1);
  or or_1 (out_7, and_1_out, and_2_out, and_3_out, and_4_out);
  or or_2 (out_8, and_5_out, and_6_out, and_7_out, and_8_out);
  or or_3 (out_9, and_9_out, and_10_out, and_11_out, and_12_out);
  or or_4 (out_10, and_13_out, and_14_out, and_15_out, and_16_out);
endmodule
