// Logisim project 数据分配器.circ as structural Verilog: 1 circuit, main circuit main
module main (
  input  in_1,
  input  in_2,
  input  in_3,
  output out_4,
  output out_5,
  output out_6,
  output out_7
);

  wire not_1_out, not_2_out;

  not not_1 (not_1_out, in_1);
  not not_2 (not_2_out, in_2);
  or or_1 (out_4, in_3, not_1_out, not_2_out);
  or or_2 (out_5, in_3, in_2, not_1_out);
  or or_3 (out_6, in_3, in_1, not_2_out);
  or or_4 (out_7, in_3, in_2, in_1);
endmodule
