// Logisim project 加法器-多路选择器型.circ as structural Verilog: 1 circuit, main circuit main
// 0
module main (
  input  [3:0] in_1,
  input  in_2,
  output [3:0] out_3,
  output out_4
);

  wire A_qn, ADD_LDB_out, adder_1_cout, and_1_out, and_2_out, and_3_out, and_4_out, and_5_out, B_qn,
       clock_1_out, CLR_out, LDA_out, LDC_out, multiplexer_1_out, multiplexer_2_out, not_1_out;
  wire [1:0] B_q;
  wire [3:0] adder_1_out, controlled_buffer_1_out, register_1_q;

  Multiplexer #(.select(2)) multiplexer_1 (
    .in0(1'b0), .in1(1'b1), .in2(1'b1), .in3(1'b1), .out(multiplexer_1_out), .sel(B_q));  // open: en
  Clock clock_1 (.out(clock_1_out));
  Multiplexer #(.select(2)) multiplexer_2 (
    .in0(1'b1), .in1(1'b1), .in2(1'b1), .in3(1'b0), .out(multiplexer_2_out), .sel(B_q));  // open: en
  not not_1 (not_1_out, clock_1_out);
  D_Flip_Flop B (.clk(clock_1_out), .D(multiplexer_1_out), .Q(B_q[0]), .Qn(B_qn));  // open: preset, en, reset
  D_Flip_Flop A (.clk(clock_1_out), .D(multiplexer_2_out), .Q(B_q[1]), .Qn(A_qn));  // open: preset, en, reset
  and and_1 (and_1_out, B_qn, A_qn);
  and and_2 (and_2_out, B_q[0], B_q[1]);
  or LDA (LDA_out, and_1_out, and_2_out);
  xor ADD_LDB (ADD_LDB_out, B_q[0], B_q[1]);
  and LDC (LDC_out, B_q[0], A_qn);
  nor CLR (CLR_out, B_q[1], B_q[0]);
  and and_3 (and_3_out, not_1_out, LDA_out);
  and and_4 (and_4_out, not_1_out, ADD_LDB_out);
  and and_5 (and_5_out, not_1_out, LDC_out);
  Register #(.width(4)) register_1 (.D(in_1), .Q(register_1_q), .clk(and_3_out));  // open: en, clr
  assign controlled_buffer_1_out = ADD_LDB_out ? out_3 : 4'bz;  // Controlled_Buffer controlled_buffer_1
  Adder #(.width(4)) adder_1 (
    .a(register_1_q), .b(controlled_buffer_1_out), .out(adder_1_out), .cin(in_2), .cout(adder_1_cout));
  Register #(.width(1)) register_2 (.D(adder_1_cout), .Q(out_4), .clk(and_5_out), .clr(CLR_out));  // open: en
  Register #(.width(4)) register_3 (.D(adder_1_out), .Q(out_3), .clk(and_4_out));  // open: en, clr
endmodule
