// Logisim project 加法器-定序型.circ as structural Verilog: 1 circuit, main circuit main
// 0
module main (
  input  [3:0] in_1,
  input  in_2,
  input  in_3,
  output [3:0] out_4,
  output out_5
);

  wire ADD_LDB_out, adder_1_cout, and_1_out, and_2_out, and_3_out, and_4_out, and_5_out, and_6_out,
       clock_1_out, CLR_out, d_ff_1_q, d_ff_1_qn, d_ff_2_q, d_ff_2_qn, d_ff_3_q, d_ff_3_qn, d_ff_4_q,
       d_ff_4_qn, LDA_out, LDC_out, not_1_out, not_2_out, not_3_out, not_4_out, not_5_out, or_1_out;
  wire [3:0] adder_1_out, controlled_buffer_1_out, register_1_q;

  not not_1 (not_1_out, d_ff_1_q);
  not not_2 (not_2_out, d_ff_2_q);
  not not_3 (not_3_out, d_ff_3_q);
  not not_4 (not_4_out, d_ff_4_q);
  Clock clock_1 (.out(clock_1_out));
  and and_1 (and_1_out, d_ff_1_q, not_2_out, not_3_out, not_4_out);
  and and_2 (and_2_out, not_1_out, d_ff_2_q, not_3_out, not_4_out);
  and and_3 (and_3_out, not_1_out, not_2_out, not_3_out, d_ff_4_q);
  and and_4 (and_4_out, not_1_out, not_2_out, d_ff_3_q, not_4_out);
  not not_5 (not_5_out, clock_1_out);
  or or_1 (or_1_out, and_2_out, and_3_out);
  D_Flip_Flop d_ff_1 (.clk(clock_1_out), .D(1'b0), .Q(d_ff_1_q), .Qn(d_ff_1_qn), .preset(in_2));  // open: en, reset
  D_Flip_Flop d_ff_2 (.clk(clock_1_out), .D(and_1_out), .Q(d_ff_2_q), .Qn(d_ff_2_qn));  // open: preset, en, reset
  D_Flip_Flop d_ff_3 (.clk(clock_1_out), .D(or_1_out), .Q(d_ff_3_q), .Qn(d_ff_3_qn));  // open: preset, en, reset
  D_Flip_Flop d_ff_4 (.clk(clock_1_out), .D(and_4_out), .Q(d_ff_4_q), .Qn(d_ff_4_qn));  // open: preset, en, reset
  and and_5 (and_5_out, not_5_out, d_ff_1_q, d_ff_2_qn, d_ff_3_qn, d_ff_4_qn);
  and and_6 (and_6_out, not_5_out, d_ff_1_qn, d_ff_2_qn, d_ff_3_q, d_ff_4_qn);
  or LDA (LDA_out, and_5_out, and_6_out);
  and LDC (LDC_out, not_5_out, d_ff_1_qn, d_ff_2_qn, d_ff_3_qn, d_ff_4_q);
  and CLR (CLR_out, d_ff_1_q, d_ff_2_qn, d_ff_3_qn, d_ff_4_qn);
  and ADD_LDB (ADD_LDB_out, not_5_out, or_1_out);
  Register #(.width(4)) register_1 (.D(in_1), .Q(register_1_q), .clk(LDA_out));  // open: en, clr
  assign controlled_buffer_1_out = or_1_out ? out_4 : 4'bz;  // Controlled_Buffer controlled_buffer_1
  Adder #(.width(4)) adder_1 (
    .a(register_1_q), .b(controlled_buffer_1_out), .out(adder_1_out), .cin(in_3), .cout(adder_1_cout));
  Register #(.width(1)) register_2 (.D(adder_1_cout), .Q(out_5), .clk(LDC_out), .clr(CLR_out));  // open: en
  Register #(.width(4)) register_3 (.D(adder_1_out), .Q(out_4), .clk(ADD_LDB_out));  // open: en, clr
endmodule
