// Logisim project 比较器-多路选择器型.circ as structural Verilog: 1 circuit, main circuit main
module main (
  input  [3:0] in_1
);

  wire and_1_out, and_2_out, clock_1_out, comparator_1_lt, d_ff_1_qn, d_ff_2_qn, multiplexer_1_out,
       multiplexer_2_out, not_1_out, xnor_1_out;
  wire [1:0] d_ff_2_q;
  wire [3:0] controlled_buffer_1_out, controlled_buffer_2_out, register_1_q, register_2_q;

  Clock clock_1 (.out(clock_1_out));
  not not_1 (not_1_out, clock_1_out);
  D_Flip_Flop d_ff_1 (
    .clk(clock_1_out), .D(multiplexer_1_out), .Q(d_ff_2_q[1]), .Qn(d_ff_1_qn));  // open: preset, en, reset
  D_Flip_Flop d_ff_2 (
    .clk(clock_1_out), .D(multiplexer_2_out), .Q(d_ff_2_q[0]), .Qn(d_ff_2_qn));  // open: preset, en, reset
  Multiplexer #(.select(2)) multiplexer_1 (
    .in0(1'b0), .in1(1'b1), .in2(comparator_1_lt), .in3(1'b1), .out(multiplexer_1_out), .sel(d_ff_2_q));  // open: en
  Multiplexer #(.select(2)) multiplexer_2 (
    .in0(1'b1), .in1(1'b1), .in2(1'b1), .in3(1'b0), .out(multiplexer_2_out), .sel(d_ff_2_q));  // open: en
  and and_1 (and_1_out, not_1_out, d_ff_1_qn, d_ff_2_q[0]);
  and and_2 (and_2_out, d_ff_2_q[1], d_ff_2_qn);
  NotExactlyOne xnor_1 (.out(xnor_1_out), .in0(not_1_out), .in1(d_ff_2_q[1]), .in2(d_ff_2_q[0]));
  Register #(.width(4)) register_1 (.D(in_1), .Q(register_1_q), .clk(xnor_1_out));  // open: en, clr
  Register #(.width(4)) register_2 (.D(register_1_q), .Q(register_2_q), .clk(and_1_out));  // open: en, clr
  assign controlled_buffer_1_out = and_2_out ? register_1_q : 4'bz;  // Controlled_Buffer controlled_buffer_1
  assign controlled_buffer_2_out = and_2_out ? register_2_q : 4'bz;  // Controlled_Buffer controlled_buffer_2
  Comparator #(.width(4)) comparator_1 (
    .a(controlled_buffer_1_out), .b(controlled_buffer_2_out), .lt(comparator_1_lt));  // open: gt, eq

  // Notes on the sheet:
  //   B
  //   A
  //   LDA
  //   LDB
  //   CAP
  //   B
  //   A
endmodule
