// Logisim project 比较器-定序型.circ as structural Verilog: 1 circuit, main circuit main
module main (
  input  [3:0] in_1
);

  wire A_q, A_qn, and_1_out, and_2_out, and_3_out, and_4_out, and_5_out, B_q, B_qn, C_q, C_qn, clock_1_out,
       comparator_1_lt, D_q, D_qn, not_1_out, not_2_out, or_1_out, or_2_out, or_3_out;
  wire [3:0] controlled_buffer_1_out, controlled_buffer_2_out, register_1_q, register_2_q;

  Clock clock_1 (.out(clock_1_out));
  not not_1 (not_1_out, clock_1_out);
  D_Flip_Flop A (.clk(clock_1_out), .D(and_1_out), .Q(A_q), .Qn(A_qn));  // open: preset, en, reset
  D_Flip_Flop B (.clk(clock_1_out), .D(or_2_out), .Q(B_q), .Qn(B_qn));  // open: preset, en, reset
  D_Flip_Flop C (.clk(clock_1_out), .D(or_3_out), .Q(C_q), .Qn(C_qn));  // open: preset, en, reset
  D_Flip_Flop D (.clk(clock_1_out), .D(C_q), .Q(D_q), .Qn(D_qn));  // open: preset, en, reset
  and and_1 (and_1_out, A_qn, B_qn, C_qn, D_qn);
  or or_1 (or_1_out, A_q, C_q);
  and and_2 (and_2_out, not_2_out, D_q);
  or or_2 (or_2_out, and_2_out, A_q);
  and and_3 (and_3_out, comparator_1_lt, D_q);
  or or_3 (or_3_out, and_3_out, B_q);
  not not_2 (not_2_out, comparator_1_lt);
  and and_4 (and_4_out, not_1_out, or_1_out);
  and and_5 (and_5_out, not_1_out, B_q);
  Register #(.width(4)) register_1 (.D(in_1), .Q(register_1_q), .clk(and_4_out));  // open: en, clr
  Register #(.width(4)) register_2 (.D(register_1_q), .Q(register_2_q), .clk(and_5_out));  // open: en, clr
  assign controlled_buffer_1_out = D_q ? register_1_q : 4'bz;  // Controlled_Buffer controlled_buffer_1
  assign controlled_buffer_2_out = D_q ? register_2_q : 4'bz;  // Controlled_Buffer controlled_buffer_2
  Comparator #(.width(4)) comparator_1 (
    .a(controlled_buffer_1_out), .b(controlled_buffer_2_out), .lt(comparator_1_lt));  // open: gt, eq

  // Notes on the sheet:
  //   LDB
  //   LDA
  //   CAP
  //   B
  //   A
endmodule
