// Logisim project 比较器-计数器型.circ as structural Verilog: 1 circuit, main circuit main
module main (
  input  [3:0] in_1
);

  wire and_1_out, and_2_out, and_3_out, clock_1_out, comparator_1_lt, d_ff_1_q, d_ff_1_qn, d_ff_2_q,
       d_ff_2_qn, not_1_out, or_1_out, or_2_out, xnor_1_out;
  wire [3:0] controlled_buffer_1_out, controlled_buffer_2_out, register_1_q, register_2_q;

  Clock clock_1 (.out(clock_1_out));
  not not_1 (not_1_out, clock_1_out);
  D_Flip_Flop d_ff_1 (.clk(clock_1_out), .D(or_2_out), .Q(d_ff_1_q), .Qn(d_ff_1_qn));  // open: preset, en, reset
  D_Flip_Flop d_ff_2 (.clk(clock_1_out), .D(or_1_out), .Q(d_ff_2_q), .Qn(d_ff_2_qn));  // open: preset, en, reset
  and and_1 (and_1_out, comparator_1_lt, d_ff_1_q);
  or or_1 (or_1_out, d_ff_1_qn, d_ff_2_qn);
  or or_2 (or_2_out, and_1_out, d_ff_2_q);
  and and_2 (and_2_out, not_1_out, d_ff_1_qn, d_ff_2_q);
  and and_3 (and_3_out, d_ff_1_q, d_ff_2_qn);
  NotExactlyOne xnor_1 (.out(xnor_1_out), .in0(not_1_out), .in1(d_ff_1_q), .in2(d_ff_2_q));
  Register #(.width(4)) register_1 (.D(in_1), .Q(register_1_q), .clk(xnor_1_out));  // open: en, clr
  Register #(.width(4)) register_2 (.D(register_1_q), .Q(register_2_q), .clk(and_2_out));  // open: en, clr
  assign controlled_buffer_1_out = and_3_out ? register_1_q : 4'bz;  // Controlled_Buffer controlled_buffer_1
  assign controlled_buffer_2_out = and_3_out ? register_2_q : 4'bz;  // Controlled_Buffer controlled_buffer_2
  Comparator #(.width(4)) comparator_1 (
    .a(controlled_buffer_1_out), .b(controlled_buffer_2_out), .lt(comparator_1_lt));  // open: gt, eq

  // Notes on the sheet:
  //   B
  //   A
  //   A>B
  //   LDA
  //   LDB
  //   CAP
  //   B
  //   A
endmodule
