// Logisim project 大作业.circ as structural Verilog: 1 circuit, main circuit main
module main (
  input  clk,
  input  reset_n,
  input  game_over,
  input  game_win,
  output INIT,
  output GAMING,
  output WIN,
  output LOSE
);

  wire and_1_out, and_2_out, and_3_out, and_4_out, d_ff_1_q, d_ff_1_qn, d_ff_2_q, d_ff_2_qn, nand_1_out,
       or_1_out, or_2_out, xnor_1_out;

  and and_1 (and_1_out, d_ff_1_q, reset_n);
  and and_2 (and_2_out, d_ff_1_qn, reset_n, game_over, d_ff_2_q);
  xnor xnor_1 (xnor_1_out, d_ff_1_q, d_ff_2_q);
  nand nand_1 (nand_1_out, game_over, game_win);
  or or_1 (or_1_out, and_1_out, and_2_out);
  and and_3 (and_3_out, xnor_1_out, reset_n);
  and and_4 (and_4_out, reset_n, d_ff_1_qn, d_ff_2_q, nand_1_out);
  or or_2 (or_2_out, and_3_out, and_4_out);
  D_Flip_Flop d_ff_1 (.clk(clk), .D(or_1_out), .Q(d_ff_1_q), .Qn(d_ff_1_qn));  // open: preset, en, reset
  D_Flip_Flop d_ff_2 (.clk(clk), .D(or_2_out), .Q(d_ff_2_q), .Qn(d_ff_2_qn));  // open: preset, en, reset
  and and_5 (INIT, d_ff_1_qn, d_ff_2_qn);
  and and_6 (GAMING, d_ff_1_qn, d_ff_2_q);
  and and_7 (WIN, d_ff_1_q, d_ff_2_qn);
  and and_8 (LOSE, d_ff_1_q, d_ff_2_q);

  // Notes on the sheet:
  //   A
  //   B
endmodule
