// Logisim project encoder_Pri.circ as structural Verilog: 1 circuit, main circuit main
module main (
  input  [9:0] in_1,
  output [3:0] out_2
);

  wire and_1_out, and_2_out, and_3_out, and_4_out, and_5_out, and_6_out, and_7_out, and_8_out, and_9_out,
       and_10_out, and_11_out, and_12_out, and_13_out, not_1_out, not_2_out, not_3_out, not_4_out, not_5_out,
       not_6_out, not_7_out, not_8_out, not_9_out, not_10_out;

  not not_1 (not_1_out, in_1[0]);
  not not_2 (not_2_out, in_1[1]);
  not not_3 (not_3_out, in_1[2]);
  not not_4 (not_4_out, in_1[3]);
  not not_5 (not_5_out, in_1[4]);
  not not_6 (not_6_out, in_1[5]);
  not not_7 (not_7_out, in_1[6]);
  not not_8 (not_8_out, in_1[7]);
  not not_9 (not_9_out, in_1[8]);
  not not_10 (not_10_out, in_1[9]);
  and and_1 (and_1_out, in_1[0], in_1[1], in_1[2], not_4_out);
  and and_2 (and_2_out, in_1[0], not_2_out);
  and and_3 (and_3_out, in_1[0], in_1[1], not_3_out);
  and and_4 (and_4_out, in_1[4], in_1[5], in_1[6], in_1[7], not_9_out);
  and and_5 (and_5_out, in_1[4], in_1[5], in_1[7], in_1[6], not_10_out);
  and and_6 (and_6_out, in_1[1], in_1[2], in_1[3], not_5_out);
  and and_7 (and_7_out, in_1[2], in_1[3], not_6_out);
  and and_8 (and_8_out, in_1[2], in_1[3], in_1[6], in_1[7], not_9_out);
  and and_9 (and_9_out, in_1[2], in_1[3], in_1[6], in_1[7], not_10_out);
  and and_10 (and_10_out, in_1[1], not_3_out);
  and and_11 (and_11_out, in_1[1], in_1[3], not_5_out);
  and and_12 (and_12_out, in_1[1], in_1[3], in_1[5], not_7_out);
  and and_13 (and_13_out, in_1[1], in_1[3], in_1[5], in_1[7], not_9_out);
  or or_1 (out_2[3], not_1_out, not_2_out, not_3_out, not_4_out, not_5_out, not_6_out, not_7_out, not_8_out);
  or or_2 (out_2[2], not_1_out, and_2_out, and_3_out, and_1_out, and_4_out, and_5_out);
  or or_3 (out_2[1], not_1_out, not_2_out, and_6_out, and_8_out, and_9_out, and_7_out);
  or or_4 (out_2[0], not_1_out, and_10_out, and_11_out, and_12_out, and_13_out);
endmodule
